# Fritzing sketch Metallifood_schematic (saved by Fritzing 0.9.3b)
breadboards: 1

parts:
  Part1 = Arduino Uno (Rev3)
  LED1 = LED - 5mm [color="Red (633nm)" part_number=red_led package="5 mm [THT]"]
  LED2 = LED - 5mm [color="Green (555nm)" part_number=green_led package="5 mm [THT]"]
  J1 = Piezo Speaker [part_number=buzzer]
  R1 = Resistor [tolerance=±5% resistance=1k package=THT]
  R2 = Resistor [tolerance=±5% resistance=1k package=THT]
  R3 = Resistor [tolerance=±5% resistance=10k package=THT]
  S1 = Momentary Switch [part_number=button package=ksa_sealed_tac_switch]

nets:
  N1: Part1.D8, J1.pin2
  N2: Part1.D2, R1.Pin_0
  N3: Part1.D3_PWM, R2.Pin_0
  N4: Part1.5V, R3.Pin_0
  N5: Part1.GND, LED1.cathode, LED2.cathode, J1.pin1
  N6: LED1.anode, R1.Pin_1
  N7: LED2.anode, R2.Pin_1
  N8: R3.Pin_1, S1.1, S1.2

notes:
  Metal detector
